// Logisim project Circuit.circ as structural Verilog: 2 circuits, main circuit Milestone 1
module Milestone_1 (
  input  [2:0] S2S1S0,
  input  WR,
  input  RD,
  input  CLR,
  input  LDAR,
  input  INC,
  input  INC_2,
  input  CLR_2,
  input  LDPC,
  input  INC_3,
  input  CLR_3,
  input  LDDR,
  input  INC_4,
  input  LDAC,
  input  CLR_4,
  input  LDIR,
  input  INC_5,
  input  CLR_5,
  input  LDTR,
  input  INC_6,
  input  CLR_6,
  input  [2:0] C2C1C0
);

  wire clock_1_out, decoder_1_out1, decoder_1_out2, decoder_1_out3, decoder_1_out4, decoder_1_out5,
       decoder_1_out6, decoder_1_out7;
  wire [7:0] AR_q;
  wire [15:0] AC_q, ALU_output, bit_extender_1_out, controlled_buffer_1_out, DR_q, IR_q, PC_q, ram_1_data,
       TR_q;

  Clock clock_1 (.out(clock_1_out));
  ALU ALU (.DR(DR_q), .AC(AC_q), .Output(ALU_output), .C2C1C0(C2C1C0));
  Counter AR (
    .load(LDAR), .D(controlled_buffer_1_out[7:0]), .count(INC), .Q(AR_q), .clk(clock_1_out), .clr(CLR));  // open: carry
  RAM #(.dataWidth(16), .bus("separate")) ram_1 (
    .addr(AR_q), .din(controlled_buffer_1_out), .data(ram_1_data), .str(WR), .sel(1'b1), .clk(clock_1_out),
    .ld(RD), .clr(1'b0));
  assign bit_extender_1_out = {{8{1'b0}}, AR_q};  // Bit_Extender bit_extender_1
  Counter #(.width(16), .max('hffff)) PC (
    .load(LDPC), .D(controlled_buffer_1_out), .count(INC_2), .Q(PC_q), .clk(clock_1_out), .clr(CLR_2));  // open: carry
  Counter #(.width(16), .max('hffff)) DR (
    .load(LDDR), .D(controlled_buffer_1_out), .count(INC_3), .Q(DR_q), .clk(clock_1_out), .clr(CLR_3));  // open: carry
  Counter #(.width(16), .max('hffff)) AC (
    .load(LDAC), .D(ALU_output), .count(INC_4), .Q(AC_q), .clk(clock_1_out), .clr(CLR_4));  // open: carry
  Counter #(.width(16), .max('hffff)) IR (
    .load(LDIR), .D(controlled_buffer_1_out), .count(INC_5), .Q(IR_q), .clk(clock_1_out), .clr(CLR_5));  // open: carry
  Counter #(.width(16), .max('hffff)) TR (
    .load(LDTR), .D(controlled_buffer_1_out), .count(INC_6), .Q(TR_q), .clk(clock_1_out), .clr(CLR_6));  // open: carry
  Decoder #(.select(3), .enable("false")) decoder_1 (
    .out1(decoder_1_out1), .out2(decoder_1_out2), .out3(decoder_1_out3), .out4(decoder_1_out4),
    .out5(decoder_1_out5), .out6(decoder_1_out6), .out7(decoder_1_out7), .sel(S2S1S0));  // open: out0
  assign controlled_buffer_1_out = decoder_1_out1 ? ram_1_data : 16'bz;  // Controlled_Buffer controlled_buffer_1
  assign controlled_buffer_1_out = decoder_1_out4 ? DR_q : 16'bz;  // Controlled_Buffer controlled_buffer_2
  assign controlled_buffer_1_out = decoder_1_out5 ? AC_q : 16'bz;  // Controlled_Buffer controlled_buffer_3
  assign controlled_buffer_1_out = decoder_1_out6 ? IR_q : 16'bz;  // Controlled_Buffer controlled_buffer_4
  assign controlled_buffer_1_out = decoder_1_out7 ? TR_q : 16'bz;  // Controlled_Buffer controlled_buffer_5
  assign controlled_buffer_1_out = decoder_1_out2 ? bit_extender_1_out : 16'bz;  // Controlled_Buffer controlled_buffer_6
  assign controlled_buffer_1_out = decoder_1_out3 ? PC_q : 16'bz;  // Controlled_Buffer controlled_buffer_7
endmodule

module ALU (
  input  [15:0] DR,
  input  [15:0] AC,
  input  [2:0] C2C1C0,
  output [15:0] Output
);

  wire [15:0] adder_1_out, divider_1_out, multiplier_1_out, not_1_out, subtractor_1_out, xor_1_out;

  assign not_1_out = ~DR;  // NOT_Gate not_1, 16 bits wide
  Adder #(.width(16)) adder_1 (.a(DR), .b(AC), .out(adder_1_out));  // open: cin, cout
  Subtractor #(.width(16)) subtractor_1 (.a(DR), .b(AC), .out(subtractor_1_out));  // open: bin, bout
  Multiplier #(.width(16)) multiplier_1 (.a(DR), .b(AC), .out(multiplier_1_out));  // open: cin, cout
  Divider #(.width(16)) divider_1 (.a(DR), .b(AC), .out(divider_1_out));  // open: upper, rem
  assign xor_1_out = DR ^ AC;  // XOR_Gate xor_1, 16 bits wide
  Multiplexer #(.select(3), .width(16)) multiplexer_1 (
    .in1(DR), .in2(adder_1_out), .in3(subtractor_1_out), .in4(multiplier_1_out), .in5(divider_1_out),
    .in6(not_1_out), .in7(xor_1_out), .out(Output), .sel(C2C1C0), .en(1'b1));  // open: in0
endmodule
